# Fritzing sketch active-buzzer (saved by Fritzing 0.9.3b)
breadboards: 1

parts:
  S1 = Pushbutton [package="[THT]"]
  J1 = Piezo Speaker
  Part1 = Arduino Uno (Rev3)

nets:
  N1: S1.Pin_1, S1.Pin_2, Part1.D2
  N2: S1.Pin_3, S1.Pin_4, J1.pin1, Part1.GND
  N3: J1.pin2, Part1.D3_PWM
